// Logisim project HW3.circ as structural Verilog
module cpu_main (
  input  in_1,
  input  in_2,
  input  in_3,
  input  in_4,
  input  in_5,
  input  [15:0] in_6,
  input  in_7,
  input  in_8,
  input  [15:0] in_9,
  input  in_10,
  output out_11,
  output out_12,
  output [3:0] out_13,
  output [2:0] out_14,
  output [15:0] out_15,
  output [15:0] out_16,
  output [2:0] out_17,
  output [15:0] out_18,
  output [4:0] out_19
);

  wire clock, clock_1_out, control_1_out_5, control_1_shut_down_halt, control_1_write, I_R,
       multiplexer_1_out, not_1_out, not_2_out, not_3_out;
  wire [2:0] r1;
  wire [15:0] adder_1_out, adder_3_out, ALUout, bit_extender_1_out, multiplexer_2_out, multiplexer_3_out,
       negator_1_out, r1_data, r2_data, register_1_q, register_3_q, undriven;
  wire [15:11] ram_1_data;

  Clock clock_1 (.out(clock_1_out));
  and and_1 (clock, clock_1_out, not_1_out);
  not not_1 (not_1_out, control_1_shut_down_halt);
  Register #(.width(16)) register_1 (.D(adder_1_out), .en(1'b1), .Q(register_1_q), .clk(clock));  // open: clr
  Adder #(.width(16)) adder_1 (.a(16'h1), .b(register_1_q), .out(adder_1_out));  // open: cin, cout
  RAM #(.addrWidth(16), .dataWidth(16), .bus("separate")) ram_1 (
    .addr(register_1_q), .data({ram_1_data, out_14, r1, out_17, out_19[1:0]}), .sel(1'b1), .ld(1'b1));  // open: din, str, clk, clr
  Multiplexer multiplexer_1 (.in0(in_3), .in1(in_5), .out(multiplexer_1_out), .sel(in_8));  // open: en
  control control_1 (
    .opcode(ram_1_data), .shut_down_halt(control_1_shut_down_halt), .write(control_1_write), .I_or_R(I_R),
    .out_5(control_1_out_5));
  assign bit_extender_1_out = {{11{1'b0}}, {out_17, out_19[1:0]}};  // Bit_Extender bit_extender_1
  Multiplexer #(.width(16)) multiplexer_2 (
    .in0(r2_data), .in1(bit_extender_1_out), .out(multiplexer_2_out), .sel(not_2_out));  // open: en
  not not_2 (not_2_out, I_R);
  not not_3 (not_3_out, control_1_out_5);
  Multiplexer #(.width(16)) multiplexer_3 (
    .in0(bit_extender_1_out), .in1(ALUout), .out(multiplexer_3_out), .sel(not_3_out));  // open: en
  Negator #(.width(16)) negator_1 (.in(in_6), .out(negator_1_out));
  ALU_q1_q2 alu_q1_q2_1 (
    .op1(r1_data), .op2(multiplexer_2_out), .opcode_decide_which_instrusion_would_be_selected(ram_1_data),
    .data_output(ALUout));
  Adder #(.width(16)) adder_2 (.a(negator_1_out), .b(in_9), .out(out_16));  // open: cin, cout
  register register_2 (
    .allow_write(control_1_write), .Write_Register_which_reg(out_14),
    .Register_Data_data_input(multiplexer_3_out), .clock_update_reg_per_clock(clock), .data_1(r1_data),
    .data_2(r2_data), .Read_Regisiter2(out_17), .Read_Regisiter1(r1));  // open: reset, in_2, in_3
  Register #(.width(16)) register_3 (.D(adder_3_out), .en(1'b1), .Q(register_3_q), .clk(clock));  // open: clr
  RAM #(.addrWidth(16), .dataWidth(16), .bus("separate")) ram_2 (
    .addr(register_3_q), .din(undriven), .data(out_18), .str(1'b1), .sel(1'b1), .clk(clock), .ld(1'b1));  // open: clr
  Adder #(.width(16)) adder_3 (.a(16'h1), .b(register_3_q), .out(adder_3_out));  // open: cin, cout

  assign out_11 = in_1;
  assign out_12 = in_1;
  assign out_13 = {in_10, in_7, in_4, in_2};
  assign out_19[4:2] = out_17;

  // Other names for the same wires on the sheet: des[2:0] = out_14; debug1[15:0] = out_15;
  //   ime[4:0] = {out_17, out_19[1:0]}; r2[2:0] = out_17; ime_data[15:0] = out_18; test = in_1

  // Notes on the sheet:
  //   debug area
  //   pc
  //   debug area
  //   debug area
endmodule

module ALU_q1_q2 (
  input  [15:0] op1,
  input  [15:0] op2,
  input  [4:0] opcode_decide_which_instrusion_would_be_selected,
  output [15:0] data_output
);

  wire [15:0] adder_1_out, and_1_out, multiplier_1_out, negator_1_out, or_1_out;

  Adder #(.width(16)) adder_1 (.a(op1), .b(op2), .out(adder_1_out));  // open: cin, cout
  Negator #(.width(16)) negator_1 (.in(op1), .out(negator_1_out));
  assign and_1_out = op1 & op2;  // AND_Gate and_1, 16 bits wide
  assign or_1_out = op1 | op2;  // OR_Gate or_1, 16 bits wide
  Multiplier #(.width(16)) multiplier_1 (.a(op1), .b(op2), .out(multiplier_1_out));  // open: cin, cout
  Multiplexer #(.select(5), .width(16)) multiplexer_1 (
    .in1(adder_1_out), .in2(negator_1_out), .in5(and_1_out), .in6(or_1_out), .in7(multiplier_1_out),
    .out(data_output), .sel(opcode_decide_which_instrusion_would_be_selected), .en(1'b1));  // open: in0, in3, in4, in8, in9, in10, in11, in12, in13, in14, in15, in16, in17, in18, in19, in20, in21, in22, in23, in24, in25, in26, in27, in28, in29, in30, in31

  // Notes on the sheet:
  //   r1
  //   r2
  //   1.li
  //   2.add
  //   3.neg
  //   4.ble
  //   5.halt
  //   6.and
  //   7.or
  //   8.mult
  //   9.load
  //   10.store
  //   11.move
endmodule

module register (
  input  allow_write,
  input  [1:0] in_2,
  input  in_3,
  input  [2:0] Read_Regisiter1,
  input  [2:0] Write_Register_which_reg,
  input  [2:0] Read_Regisiter2,
  input  reset,
  input  [15:0] Register_Data_data_input,
  input  clock_update_reg_per_clock,
  output [15:0] data_1,
  output [15:0] data_2
);

  wire and_1_out, and_2_out, and_3_out, and_4_out, and_5_out, and_6_out, and_7_out, and_8_out, clock_1_out,
       decoder_1_out0, decoder_1_out1, decoder_1_out2, decoder_1_out3, decoder_2_out0, decoder_2_out1,
       decoder_2_out2, decoder_2_out3, decoder_2_out4, decoder_2_out5, decoder_2_out6, decoder_2_out7;
  wire [15:0] register_1_q, register_2_q, register_3_q, register_4_q, register_5_q, register_6_q,
       register_7_q, register_8_q, register_9_q, undriven;

  Decoder #(.select(2), .enable("false")) decoder_1 (
    .out0(decoder_1_out0), .out1(decoder_1_out1), .out2(decoder_1_out2), .out3(decoder_1_out3), .sel(in_2));
  Clock clock_1 (.out(clock_1_out));
  Register #(.width(16)) register_1 (.D(undriven), .en(in_3), .Q(register_1_q), .clk(clock_1_out));  // open: clr
  Decoder #(.select(3), .enable("false")) decoder_2 (
    .out0(decoder_2_out0), .out1(decoder_2_out1), .out2(decoder_2_out2), .out3(decoder_2_out3),
    .out4(decoder_2_out4), .out5(decoder_2_out5), .out6(decoder_2_out6), .out7(decoder_2_out7),
    .sel(Write_Register_which_reg));
  and and_1 (and_1_out, allow_write, decoder_2_out0);
  and and_2 (and_2_out, allow_write, decoder_2_out1);
  and and_3 (and_3_out, allow_write, decoder_2_out2);
  and and_4 (and_4_out, allow_write, decoder_2_out3);
  and and_5 (and_5_out, allow_write, decoder_2_out4);
  and and_6 (and_6_out, allow_write, decoder_2_out5);
  and and_7 (and_7_out, allow_write, decoder_2_out6);
  and and_8 (and_8_out, allow_write, decoder_2_out7);
  Register #(.width(16)) register_2 (
    .D(Register_Data_data_input), .en(and_1_out), .Q(register_2_q), .clk(clock_update_reg_per_clock),
    .clr(reset));
  Register #(.width(16)) register_3 (
    .D(Register_Data_data_input), .en(and_2_out), .Q(register_3_q), .clk(clock_update_reg_per_clock),
    .clr(reset));
  Register #(.width(16)) register_4 (
    .D(Register_Data_data_input), .en(and_3_out), .Q(register_4_q), .clk(clock_update_reg_per_clock),
    .clr(reset));
  Register #(.width(16)) register_5 (
    .D(Register_Data_data_input), .en(and_4_out), .Q(register_5_q), .clk(clock_update_reg_per_clock),
    .clr(reset));
  Register #(.width(16)) register_6 (
    .D(Register_Data_data_input), .en(and_5_out), .Q(register_6_q), .clk(clock_update_reg_per_clock),
    .clr(reset));
  Register #(.width(16)) register_7 (
    .D(Register_Data_data_input), .en(and_6_out), .Q(register_7_q), .clk(clock_update_reg_per_clock),
    .clr(reset));
  Register #(.width(16)) register_8 (
    .D(Register_Data_data_input), .en(and_7_out), .Q(register_8_q), .clk(clock_update_reg_per_clock),
    .clr(reset));
  Register #(.width(16)) register_9 (
    .D(Register_Data_data_input), .en(and_8_out), .Q(register_9_q), .clk(clock_update_reg_per_clock),
    .clr(reset));
  Multiplexer #(.select(3), .width(16), .enable("false")) multiplexer_1 (
    .in0(register_2_q), .in1(register_3_q), .in2(register_4_q), .in3(register_5_q), .in4(register_6_q),
    .in5(register_7_q), .in6(register_8_q), .in7(register_9_q), .out(data_1), .sel(Read_Regisiter1));
  Multiplexer #(.select(3), .width(16), .enable("false")) multiplexer_2 (
    .in0(register_2_q), .in1(register_3_q), .in2(register_4_q), .in3(register_5_q), .in4(register_6_q),
    .in5(register_7_q), .in6(register_8_q), .in7(register_9_q), .out(data_2), .sel(Read_Regisiter2));
endmodule

module control (
  input  [4:0] opcode,
  output shut_down_halt,
  output write,
  output I_or_R,
  output out_5
);

  wire _2_out, _3_out, _4_out, _6_out, _7_out, _8_out, _9_out, _10_out, _11_out, _12_out, _13_out, _14_out,
       _15_out, _16_out, or_1_out;

  and _1 (out_5, ~opcode[4], ~opcode[3], ~opcode[2], ~opcode[1], ~opcode[0]);  // AND_Gate
  and _2 (_2_out, ~opcode[4], ~opcode[3], ~opcode[2], ~opcode[1], opcode[0]);  // AND_Gate
  and _3 (_3_out, ~opcode[4], ~opcode[3], ~opcode[2], opcode[1], ~opcode[0]);  // AND_Gate
  and _4 (_4_out, ~opcode[4], ~opcode[3], ~opcode[2], opcode[1], opcode[0]);  // AND_Gate
  and _5 (shut_down_halt, ~opcode[4], ~opcode[3], opcode[2], ~opcode[1], ~opcode[0]);  // AND_Gate
  and _6 (_6_out, ~opcode[4], ~opcode[3], opcode[2], ~opcode[1], opcode[0]);  // AND_Gate
  and _7 (_7_out, ~opcode[4], ~opcode[3], opcode[2], opcode[1], ~opcode[0]);  // AND_Gate
  and _8 (_8_out, ~opcode[4], ~opcode[3], opcode[2], opcode[1], opcode[0]);  // AND_Gate
  and _9 (_9_out, ~opcode[4], opcode[3], ~opcode[2], ~opcode[1], ~opcode[0]);  // AND_Gate
  and _10 (_10_out, ~opcode[4], opcode[3], ~opcode[2], ~opcode[1], opcode[0]);  // AND_Gate
  and _11 (_11_out, ~opcode[4], opcode[3], ~opcode[2], opcode[1], ~opcode[0]);  // AND_Gate
  and _12 (_12_out, ~opcode[4], opcode[3], ~opcode[2], opcode[1], opcode[0]);  // AND_Gate
  and _13 (_13_out, ~opcode[4], opcode[3], opcode[2], ~opcode[1], ~opcode[0]);  // AND_Gate
  and _14 (_14_out, ~opcode[4], opcode[3], opcode[2], ~opcode[1], opcode[0]);  // AND_Gate
  and _15 (_15_out, ~opcode[4], opcode[3], opcode[2], opcode[1], ~opcode[0]);  // AND_Gate
  and _16 (_16_out, ~opcode[4], opcode[3], opcode[2], opcode[1], opcode[0]);  // AND_Gate
  buf or_1 (or_1_out, _9_out);  // OR_Gate
  not not_1 (write, or_1_out);
  or or_2 (I_or_R, _2_out, _3_out);

  // Other names for the same wires on the sheet: _0 = opcode[0]; _1 = opcode[1]; _2 = opcode[2]; _3 = opcode[3];
  //   _4 = opcode[4]

  // Notes on the sheet:
  //   out 0 == I type ; 1== R type
  //   li instrusion?
  //   1.li
  //   2.add
  //   3.neg
  //   4.ble
  //   5.halt
  //   6.and
  //   7.or
  //   8.mult
  //   9.load
  //   10.store
  //   11.move
endmodule
